# Fritzing sketch tanks (saved by Fritzing 0.9.5d)
breadboards: 1

parts:
  Composant1 = Arduino Uno (Rev3)
  hc-sr1 = hc-sr04
  hc-sr2 = hc-sr04
  J1 = Basic Force Sensing Resistor (FSR) [package=THT]
  S4 = SPST Switch [package=switch-spdt]
  R1 = Resistor [tolerance=±5% resistance=220 package=THT]
  RE1 = KY-040 Rotary encoder [package=THT]
  Composant3 = NeoPixel Stick [part_number=1426]
  R2 = Resistor [tolerance=±5% resistance=220 package=THT]

nets:
  N1: Composant1.A0, J1.pin_0, R1.Pin_1
  N2: Composant1.D8, R2.Pin_0
  N3: Composant1.D9_PWM, hc-sr2.Echo
  N4: Composant1.D10_PWM/SS, hc-sr2.Trig
  N5: Composant1.D11_PWM/MOSI, RE1.SW
  N6: Composant1.D2, RE1.CLK
  N7: Composant1.D3_PWM, RE1.DT
  N8: Composant1.D5_PWM, hc-sr1.Echo
  N9: Composant1.D6_PWM, hc-sr1.Trig
  N10: Composant1.D7, S4.P
  VCC: Composant1.5V, hc-sr1.VCC, hc-sr2.VCC, R1.Pin_0, RE1.Vcc, Composant3.+5V
  GND: Composant1.GND, hc-sr1.GND, hc-sr2.GND, J1.pin_1, S4.S, RE1.GND, Composant3.GND
  N11: Composant3.DATAOUT, R2.Pin_1

custom parts:
  KY-040 Rotary encoder: KY-040 Rotary Encoder with switch on breakout borad from AZ Delivery
  NeoPixel Stick: Make your own little LED strip arrangement with this stick of NeoPixel LEDs. We crammed 8 of the tiny 5050 (5mm x 5mm) smart RGB LEDs onto a PCB with mounting holes and a chainable design. Use only one microcontroller pin to control as many as you can chain together! Each LED is addressable as the driver chip is inside the LED. Each one has ~18mA constant current drive so the color will be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
